# Fritzing sketch break_beam_alarm-V1 (saved by Fritzing 0.9.2b)
perfboards: 1

parts:
  Raspberry_Pi1 = Raspberry Pi B+
  IC1 = MCP3008 8-channel 10-bit ADC [part_number=MCP3008]
  R2 = Photocell (LDR) [package=THT]
  LD2 = LD
  S1 = Pushbutton [package="[THT]"]
  R4 = Resistor [tolerance=±5% resistance=10k package=THT]
  R5 = Resistor [tolerance=±5% resistance=10k package=THT]
  R6 = Photocell (LDR) [package=THT]
  LD4 = LD
  LED1 = LED - 5mm [color="Yellow (585nm)" package="5 mm [THT]"]
  LED2 = LED - 5mm [color="Green (555nm)" package="5 mm [THT]"]
  LED3 = LED - 5mm [color="Yellow (592nm)" package="5 mm [THT]"]
  LED4 = LED - 5mm [color="Red (633nm)" package="5 mm [THT]"]
  S2 = Pushbutton [package="[THT]"]
  S3 = Pushbutton [package="[THT]"]
  R7 = Resistor [tolerance=±5% resistance=10k package=THT]
  R8 = Resistor [tolerance=±5% resistance=10k package=THT]
  R9 = Resistor [tolerance=±5% resistance=10k package=THT]
  R10 = Resistor [tolerance=±5% resistance=10k package=THT]

nets:
  N1: Raspberry_Pi1.3v3, IC1.no_name_yet#15, IC1.no_name_yet#16, R2.pin_0, LD2.anode, S1.Pin_1, S1.Pin_2, R6.pin_0, S2.Pin_1, S2.Pin_2, S3.Pin_3, S3.Pin_4, R9.Pin_0, R10.Pin_0
  N2: Raspberry_Pi1.GPIO2, LD2.cathode, LED2.cathode
  N3: Raspberry_Pi1.GPIO3, LD4.cathode, LED1.anode
  N4: Raspberry_Pi1.GPIO4, S3.Pin_1, S3.Pin_2
  N5: Raspberry_Pi1.GPIO17, S1.Pin_3, S1.Pin_4
  N6: Raspberry_Pi1.GPIO10, IC1.no_name_yet#11
  N7: Raspberry_Pi1.GPIO9, IC1.no_name_yet#12
  N8: Raspberry_Pi1.GPIO11, IC1.no_name_yet#13
  N9: Raspberry_Pi1.GND, R4.Pin_1
  N10: Raspberry_Pi1.GPIO8, IC1.no_name_yet#10
  N11: Raspberry_Pi1.GPIO18, S2.Pin_4
  N12: Raspberry_Pi1.GPIO15, LED4.cathode
  N13: Raspberry_Pi1.GPIO14, LED3.cathode
  N14: IC1.no_name_yet#1, R5.Pin_0, R6.pin_1
  N15: IC1.no_name_yet#2, R2.pin_1, R4.Pin_0
  N16: IC1.no_name_yet#9, IC1.no_name_yet#14, R5.Pin_1
  N17: LD4.anode, R7.Pin_1
  N18: LED1.cathode, R7.Pin_0, R8.Pin_0
  N19: LED2.anode, R8.Pin_1
  N20: LED3.anode, R10.Pin_1
  N21: LED4.anode, R9.Pin_1

custom parts:
  LD: A Generic Red Dot Laser Diode Module (~5mW)
